// Logisim project riscv32.circ as structural Verilog: 2 circuits, main circuit main
module main (
  input  in_1
);

  wire alu_1_out_3, clock_1_out;

  Clock clock_1 (.out(clock_1_out));
  alu alu_1 (.a(clock_1_out), .b(in_1), .out_3(alu_1_out_3));
  LED led_1 (.in(alu_1_out_3));
endmodule

module alu (
  input  a,
  input  b,
  output out_3
);

  and and_1 (out_3, a, b);

  // Notes on the sheet:
  //   AND
  //   out
endmodule
